// Logisim project 3_bit_and.circ as structural Verilog: 1 circuit, main circuit main
module main (
  input  [2:0] in_1,
  input  [2:0] in_2,
  output out_3
);

  wire nand_1_out, nand_2_out, nand_3_out, nand_4_out;

  nand nand_1 (nand_1_out, in_1[0], in_2[0]);
  nand nand_2 (nand_2_out, in_1[1], in_2[1]);
  nand nand_3 (nand_3_out, in_1[2], in_2[2]);
  nand nand_4 (nand_4_out, nand_1_out, nand_2_out);
  nand nand_5 (out_3, nand_4_out, nand_3_out);
endmodule
