// Digital circuit or.dig as structural Verilog
module \or  (
  input  A,
  input  B,
  output Y
);

  wire not_1_out, not_2_out;

  not not_1 (not_1_out, A);
  not not_2 (not_2_out, B);
  nand nand_1 (Y, not_1_out, not_2_out);
endmodule
